// Logisim project item_d.circ as structural Verilog: 1 circuit, main circuit circ_d
module circ_d (
  input  A,
  input  B,
  input  C,
  output x,
  output y
);

  wire and_1_out, and_2_out, or_1_out, or_2_out;

  xor odd_parity_1 (x, A, B, C);
  and and_1 (and_1_out, A, B);
  or or_1 (or_1_out, and_1_out, B);
  and and_2 (and_2_out, or_1_out, C);
  or or_2 (or_2_out, and_2_out, A);
  and and_3 (y, or_2_out, C);
endmodule
