// Logisim project item_a.circ as structural Verilog: 1 circuit, main circuit circ_a
module circ_a (
  input  A,
  input  B,
  input  C,
  output X
);

  wire not_1_out, not_2_out, or_1_out;

  not not_1 (not_1_out, A);
  not not_2 (not_2_out, B);
  or or_1 (or_1_out, not_1_out, not_2_out);
  and and_1 (X, or_1_out, B, C);
endmodule
