// Logisim project questao04.circ as structural Verilog: 1 circuit, main circuit main
module main (
  input  F,
  input  U,
  input  T,
  input  H,
  output A
);

  wire and_1_out, and_2_out;

  and and_1 (and_1_out, F, U);
  and and_2 (and_2_out, T, H);
  or or_1 (A, and_1_out, and_2_out);
endmodule
