// Logisim project questao05.circ as structural Verilog: 1 circuit, main circuit main
module main (
  input  [2:0] B,
  output [3:0] Y
);

  wire and_3_out, and_4_out, and_5_out, not_1_out, not_2_out, not_3_out;

  not not_1 (not_1_out, B[2]);
  not not_2 (not_2_out, B[1]);
  not not_3 (not_3_out, B[0]);
  and and_1 (Y[3], B[2], B[1]);
  and and_2 (Y[2], B[2], not_2_out);
  and and_3 (and_3_out, not_1_out, not_2_out, not_3_out);
  and and_4 (and_4_out, B[1], B[0]);
  and and_5 (and_5_out, B[2], B[0]);
  or or_1 (Y[1], and_3_out, and_4_out, and_5_out);

  assign Y[0] = 1'b1;
endmodule
